// Logisim project 2^n mod 5.circ as structural Verilog: 3 circuits, main circuit mod5
module mod5 (
  input  in_1,
  output out_2,
  output out_3,
  output out_4,
  output out_5,
  output out_6
);

  wire clock_1_out;
  wire [1:0] register_1_q, \状态转移_1_b_ ;

  \状态转移  \u_状态转移_1  (.A(register_1_q[0]), .B(register_1_q[1]), .In(in_1), .A_(\状态转移_1_b_ [1]), .B_(\状态转移_1_b_ [0]));
  // Probe on \状态转移_1_b_ 
  Register #(.width(2)) register_1 (.D(\状态转移_1_b_ ), .en(1'b1), .Q(register_1_q), .clk(clock_1_out));  // open: clr
  Clock clock_1 (.out(clock_1_out));
  // Probe on register_1_q
  \状态输出  \u_状态输出_1  (
    .A(register_1_q[0]), .B(register_1_q[1]), .In(in_1), .S0(out_2), .S1(out_3), .S2(out_4), .S3(out_5),
    .S4(out_6));
endmodule

module \状态转移  (
  input  A,
  input  B,
  input  In,
  output A_,
  output B_
);

  wire and_1_out, and_2_out, and_3_out, and_4_out, and_5_out, and_6_out, not_1_out, not_2_out, not_3_out,
       not_4_out, not_5_out, not_6_out, not_7_out, not_8_out;

  not not_1 (not_1_out, A);
  not not_2 (not_2_out, B);
  not not_3 (not_3_out, A);
  not not_4 (not_4_out, B);
  not not_5 (not_5_out, A);
  not not_6 (not_6_out, In);
  not not_7 (not_7_out, B);
  not not_8 (not_8_out, In);
  and and_1 (and_1_out, not_1_out, B);
  and and_2 (and_2_out, A, not_2_out);
  and and_3 (and_3_out, not_3_out, not_4_out, In);
  and and_4 (and_4_out, not_5_out, B, not_6_out);
  and and_5 (and_5_out, A, not_7_out, not_8_out);
  and and_6 (and_6_out, A, B, In);
  or or_1 (A_, and_1_out, and_2_out);
  or or_2 (B_, and_3_out, and_4_out, and_5_out, and_6_out);
endmodule

module \状态输出  (
  input  A,
  input  B,
  input  In,
  output S0,
  output S1,
  output S2,
  output S3,
  output S4
);

  wire and_1_out, and_2_out, and_3_out, and_4_out, and_5_out, and_6_out, and_7_out, and_8_out, not_1_out,
       not_2_out, not_3_out, not_4_out, not_5_out, not_6_out, not_7_out, not_8_out, not_9_out, not_10_out,
       not_11_out, not_12_out;

  not not_1 (not_1_out, A);
  not not_2 (not_2_out, B);
  not not_3 (not_3_out, In);
  not not_4 (not_4_out, In);
  not not_5 (not_5_out, A);
  not not_6 (not_6_out, B);
  not not_7 (not_7_out, A);
  not not_8 (not_8_out, B);
  not not_9 (not_9_out, A);
  not not_10 (not_10_out, In);
  not not_11 (not_11_out, B);
  not not_12 (not_12_out, In);
  and and_1 (and_1_out, not_1_out, not_2_out, not_3_out);
  and and_2 (and_2_out, A, B, not_4_out);
  and and_3 (and_3_out, not_5_out, not_6_out, In);
  and and_4 (and_4_out, A, B, In);
  and and_5 (and_5_out, not_7_out, B, In);
  and and_6 (and_6_out, A, not_8_out, In);
  and and_7 (and_7_out, not_9_out, B, not_10_out);
  and and_8 (and_8_out, A, not_11_out, not_12_out);
  or or_1 (S1, and_1_out, and_2_out);
  or or_2 (S2, and_3_out, and_4_out);
  or or_3 (S3, and_5_out, and_6_out);
  or or_4 (S4, and_7_out, and_8_out);

  assign S0 = 1'b0;
endmodule
