// Logisim project 4BitSort.circ as structural Verilog: 4 circuits, main circuit 4bit_sort
module _4bit_sort (
  input  [3:0] A,
  input  [3:0] B,
  input  [3:0] C,
  input  [3:0] D,
  output [3:0] _1,
  output [3:0] _2,
  output [3:0] _3,
  output [3:0] _4
);

  wire [3:0] if_lafer_1_o1, if_lafer_1_o2, if_lafer_2_o1, if_lafer_2_o2, if_lafer_3_o1, if_lafer_4_o1,
       if_lafer_4_o2, if_lafer_5_o1;

  IF_LAFER if_lafer_1 (.L1(A), .L2(B), .O1(if_lafer_1_o1), .O2(if_lafer_1_o2));
  IF_LAFER if_lafer_2 (.L1(if_lafer_1_o2), .L2(C), .O1(if_lafer_2_o1), .O2(if_lafer_2_o2));
  IF_LAFER if_lafer_3 (.L1(if_lafer_2_o2), .L2(D), .O1(if_lafer_3_o1), .O2(_4));
  IF_LAFER if_lafer_4 (.L1(if_lafer_1_o1), .L2(if_lafer_2_o1), .O1(if_lafer_4_o1), .O2(if_lafer_4_o2));
  IF_LAFER if_lafer_5 (.L1(if_lafer_4_o2), .L2(if_lafer_3_o1), .O1(if_lafer_5_o1), .O2(_3));
  IF_LAFER if_lafer_6 (.L1(if_lafer_4_o1), .L2(if_lafer_5_o1), .O1(_1), .O2(_2));
endmodule

module _4bit_swap (
  input  [3:0] L1,
  input  [3:0] L2,
  input  S,
  output [3:0] O1,
  output [3:0] O2
);

  _1bit_swap u_1bit_swap_1 (.l1(L1[0]), .l2(L2[0]), .s(S), .o1(O1[0]), .o2(O2[0]));
  _1bit_swap u_1bit_swap_2 (.l1(L1[1]), .l2(L2[1]), .s(S), .o1(O1[1]), .o2(O2[1]));
  _1bit_swap u_1bit_swap_3 (.l1(L1[2]), .l2(L2[2]), .s(S), .o1(O1[2]), .o2(O2[2]));
  _1bit_swap u_1bit_swap_4 (.l1(L1[3]), .l2(L2[3]), .s(S), .o1(O1[3]), .o2(O2[3]));

  // Other names for the same wires on the sheet: L1_0 = L1[0]; L1_1 = L1[1]; L1_2 = L1[2]; L1_3 = L1[3]; L2_0 = L2[0];
  //   L2_1 = L2[1]; L2_2 = L2[2]; L2_3 = L2[3]; O1_0 = O1[0]; O1_1 = O1[1]; O1_2 = O1[2]; O1_3 = O1[3]; O2_0 = O2[0];
  //   O2_1 = O2[1]; O2_2 = O2[2]; O2_3 = O2[3]; S1 = S
endmodule

module _1bit_swap (
  input  l1,
  input  l2,
  input  s,
  output o1,
  output o2
);

  wire and_1_out, and_2_out, and_3_out, and_4_out, not_1_out, not_2_out;

  not not_1 (not_1_out, s);
  not not_2 (not_2_out, s);
  and and_1 (and_1_out, l2, s);
  and and_2 (and_2_out, l1, not_1_out);
  and and_3 (and_3_out, l2, not_2_out);
  and and_4 (and_4_out, l1, s);
  or or_1 (o1, and_1_out, and_2_out);
  or or_2 (o2, and_3_out, and_4_out);
endmodule

module IF_LAFER (
  input  [3:0] L1,
  input  [3:0] L2,
  output [3:0] O1,
  output [3:0] O2
);

  wire comparator_1_gt;

  Comparator #(.width(4), .mode("unsigned")) comparator_1 (.a(L1), .b(L2), .gt(comparator_1_gt));  // open: eq, lt
  _4bit_swap u_4bit_swap_1 (.L1(L1), .L2(L2), .S(comparator_1_gt), .O1(O1), .O2(O2));
endmodule
