// Logisim project CRC.circ as structural Verilog: 3 circuits, main circuit CRC
module CRC (
  input  [7:0] A,
  input  [3:0] B,
  output [10:0] C
);

  wire \四位模二除法器0_3_d , \四位模二除法器1_4_d , \四位模二除法器2_5_d , \四位模二除法器3_6_d , \四位模二除法器4_7_d , \四位模二除法器5_8_d ,
       \四位模二除法器6_9_d , \四位模二除法器7_10_d ;
  wire [2:0] \四位模二除法器1_4_c , \四位模二除法器2_5_c , \四位模二除法器4_7_c , \四位模二除法器5_8_c , \四位模二除法器6_9_c , \四位模二除法器7_10_c ;
  wire [3:1] \四位模二除法器3_6_c ;

  \四位模二除法器  \u_四位模二除法器7_10  (.A(A[7:4]), .B(B), .D(\四位模二除法器7_10_d ), .C(\四位模二除法器7_10_c ));
  \四位模二除法器  \u_四位模二除法器6_9  (.A({\四位模二除法器7_10_c , A[3]}), .B(B), .D(\四位模二除法器6_9_d ), .C(\四位模二除法器6_9_c ));
  \四位模二除法器  \u_四位模二除法器5_8  (.A({\四位模二除法器6_9_c , A[2]}), .B(B), .D(\四位模二除法器5_8_d ), .C(\四位模二除法器5_8_c ));
  \四位模二除法器  \u_四位模二除法器4_7  (.A({\四位模二除法器5_8_c , A[1]}), .B(B), .D(\四位模二除法器4_7_d ), .C(\四位模二除法器4_7_c ));
  \四位模二除法器  \u_四位模二除法器3_6  (.A({\四位模二除法器4_7_c , A[0]}), .B(B), .D(\四位模二除法器3_6_d ), .C(\四位模二除法器3_6_c ));
  \四位模二除法器  \u_四位模二除法器2_5  (.A({\四位模二除法器3_6_c , 1'b0}), .B(B), .D(\四位模二除法器2_5_d ), .C(\四位模二除法器2_5_c ));
  \四位模二除法器  \u_四位模二除法器1_4  (.A({\四位模二除法器2_5_c , 1'b0}), .B(B), .D(\四位模二除法器1_4_d ), .C(\四位模二除法器1_4_c ));
  \四位模二除法器  \u_四位模二除法器0_3  (.A({\四位模二除法器1_4_c , 1'b0}), .B(B), .D(\四位模二除法器0_3_d ), .C(C[2:0]));

  assign C[10:3] = A;

  // Other names for the same wires on the sheet: _3 = A[0]; _4 = A[1]; _5 = A[2]; _6 = A[3]; _7 = A[4]; _8 = A[5];
  //   _9 = A[6]; _10 = A[7]
endmodule

module \四位模二除法器  (
  input  [3:0] A,
  input  [3:0] B,
  output D,
  output [2:0] C
);

  wire [2:0] \三位异或运算_1_c ;

  \三位异或运算  \u_三位异或运算_1  (.A(A[2:0]), .B(B[2:0]), .C(\三位异或运算_1_c ));
  Multiplexer #(.width(3), .enable("false")) multiplexer_1 (.in0(A[2:0]), .in1(\三位异或运算_1_c ), .out(C), .sel(A[3]));

  assign D = A[3];

  // Other names for the same wires on the sheet: select = A[3]
endmodule

module \三位异或运算  (
  input  [2:0] A,
  input  [2:0] B,
  output [2:0] C
);

  xor xor_1 (C[0], A[0], B[0]);
  xor xor_2 (C[1], A[1], B[1]);
  xor xor_3 (C[2], A[2], B[2]);

  // Other names for the same wires on the sheet: A_0 = A[0]; A_1 = A[1]; A_2 = A[2]; B_0 = B[0]; B_1 = B[1];
  //   B_2 = B[2]
endmodule
