// Logisim project fib.circ as structural Verilog: 3 circuits, main circuit main
module main (
  input  [2:0] in_1,
  output [3:0] out_2
);

  wire \output ;
  wire [3:0] fibnow;

  \计算逻辑  \u_计算逻辑_1  (.in_1(\output ), .out_2(fibnow));
  \计数逻辑  \u_计数逻辑_1  (.\input (in_1), .out_2(\output ));
  Multiplexer #(.width(4)) multiplexer_1 (.in0(4'b0000), .in1(fibnow), .out(out_2), .sel(\output ));  // open: en
endmodule

module \计数逻辑  (
  input  [2:0] \input ,
  output out_2
);

  wire clock_1_out;
  wire [3:0] bit_extender_1_out, counter_1_q;

  Clock clock_1 (.out(clock_1_out));
  assign bit_extender_1_out = {{1{1'b0}}, \input };  // Bit_Extender bit_extender_1
  Counter #(.width(4), .max('hf), .ongoal("stay")) counter_1 (
    .Q(counter_1_q), .clk(clock_1_out));  // open: load, D, count, carry, clr
  Comparator #(.width(4), .mode("unsigned")) comparator_1 (
    .a(bit_extender_1_out), .b(counter_1_q), .lt(out_2));  // open: gt, eq
endmodule

module \计算逻辑  (
  input  in_1,
  output [3:0] out_2
);

  wire clk, enable, initialize, undriven;
  wire [3:0] adder_1_out, multiplexer_1_out, prev;

  Clock clock_1 (.out(clk));
  Counter #(.width(1), .max('h1), .ongoal("stay")) counter_1 (
    .Q(initialize), .clk(clk));  // open: load, D, count, carry, clr
  not not_1 (enable, in_1);
  Adder #(.width(4)) adder_1 (.a(out_2), .b(prev), .out(adder_1_out));  // open: cin, cout
  Multiplexer #(.width(4)) multiplexer_1 (
    .in0(4'b0001), .in1(out_2), .out(multiplexer_1_out), .sel(initialize), .en(undriven));
  Register #(.width(4)) register_1 (.D(adder_1_out), .en(enable), .Q(out_2), .clk(clk));  // open: clr
  Register #(.width(4)) register_2 (.D(multiplexer_1_out), .en(enable), .Q(prev), .clk(clk));  // open: clr

  // Other names for the same wires on the sheet: now[3:0] = out_2
endmodule
