// Logisim project fibonacci_1.circ as structural Verilog: 3 circuits, main circuit main
module main (
  input  [2:0] in_1,
  output [3:0] out_2
);

  wire \计数逻辑_1_out_2 ;
  wire [3:0] \计算逻辑_1_out_2 ;

  \计数逻辑  \u_计数逻辑_1  (.\input (in_1), .out_2(\计数逻辑_1_out_2 ));
  \计算逻辑  \u_计算逻辑_1  (.freeze(\计数逻辑_1_out_2 ), .out_2(\计算逻辑_1_out_2 ));
  // Probe on \计算逻辑_1_out_2 
  Multiplexer #(.width(4)) multiplexer_1 (
    .in0(4'b0000), .in1(\计算逻辑_1_out_2 ), .out(out_2), .sel(\计数逻辑_1_out_2 ));  // open: en
endmodule

module \计算逻辑  (
  input  freeze,
  output [3:0] out_2
);

  wire clk, counter_1_q, not_1_out;
  wire [3:0] adder_1_out, multiplexer_1_out, prev_q;

  Clock clock_1 (.out(clk));
  Counter #(.width(1), .max('h1), .ongoal("stay")) counter_1 (
    .Q(counter_1_q), .clk(clk));  // open: load, D, count, carry, clr
  Multiplexer #(.width(4)) multiplexer_1 (
    .in0(4'b0001), .in1(out_2), .out(multiplexer_1_out), .sel(counter_1_q));  // open: en
  not not_1 (not_1_out, freeze);
  Register #(.width(4)) prev (.D(multiplexer_1_out), .en(not_1_out), .Q(prev_q), .clk(clk));  // open: clr
  Adder #(.width(4)) adder_1 (.a(out_2), .b(prev_q), .out(adder_1_out));  // open: cin, cout
  Register #(.width(4)) now (.D(adder_1_out), .en(not_1_out), .Q(out_2), .clk(clk));  // open: clr
endmodule

module \计数逻辑  (
  input  [2:0] \input ,
  output out_2
);

  wire clock_1_out;
  wire [3:0] bit_extender_1_out, counter_1_q;

  assign bit_extender_1_out = {{1{1'b0}}, \input };  // Bit_Extender bit_extender_1
  Counter #(.width(4), .max('hf), .ongoal("stay")) counter_1 (
    .Q(counter_1_q), .clk(clock_1_out));  // open: load, D, count, carry, clr
  Clock clock_1 (.out(clock_1_out));
  Comparator #(.width(4), .mode("unsigned")) comparator_1 (
    .a(bit_extender_1_out), .b(counter_1_q), .lt(out_2));  // open: gt, eq
endmodule
