// Logisim project fsm.circ as structural Verilog: 3 circuits, main circuit fsm
module fsm (
  input  CLR,
  input  [1:0] In,
  output Z
);

  wire clock_1_out;
  wire [1:0] multiplexer_1_out, register_1_q, \状态转移2_1_d0 ;

  \状态转移2  \u_状态转移2_1  (
    .input_1(In[1]), .input_0(In[0]), .Q1(register_1_q[1]), .Q0(register_1_q[0]), .D1(\状态转移2_1_d0 [1]),
    .D0(\状态转移2_1_d0 [0]));
  Multiplexer #(.width(2)) multiplexer_1 (
    .in0(\状态转移2_1_d0 ), .in1(2'b00), .out(multiplexer_1_out), .sel(CLR));  // open: en
  Register #(.width(2)) register_1 (.D(multiplexer_1_out), .Q(register_1_q), .clk(clock_1_out));  // open: en, clr
  Clock clock_1 (.out(clock_1_out));
  \输出逻辑  \u_输出逻辑_1  (.input_1(In[1]), .input_0(In[0]), .status_1(register_1_q[1]), .status_0(register_1_q[0]), .Z(Z));
endmodule

module \输出逻辑  (
  input  input_1,
  input  input_0,
  input  status_1,
  input  status_0,
  output Z
);

  wire not_1_out;

  not not_1 (not_1_out, input_0);
  and and_1 (Z, not_1_out, status_1);
endmodule

module \状态转移2  (
  input  input_1,
  input  input_0,
  input  Q1,
  input  Q0,
  output D1,
  output D0
);

  wire and_2_out, and_3_out, not_1_out, not_2_out, not_3_out, not_4_out, not_5_out;

  not not_1 (not_1_out, input_0);
  not not_2 (not_2_out, Q1);
  and and_1 (D1, not_1_out, not_2_out, Q0);
  not not_3 (not_3_out, input_1);
  not not_4 (not_4_out, input_0);
  not not_5 (not_5_out, Q1);
  and and_2 (and_2_out, not_3_out, input_0);
  or or_1 (D0, and_2_out, and_3_out);
  and and_3 (and_3_out, input_1, not_4_out, not_5_out, Q0);
endmodule
