// Logisim project ftoi.circ as structural Verilog: 1 circuit, main circuit ftoi
module ftoi (
  input  [15:0] float,
  output [31:0] \int 
);

  wire comparator_1_lt, comparator_2_eq, not_2_out, or_1_out, select;
  wire [4:0] subtractor_1_out;
  wire [31:0] adder_1_out, bit_extender_1_out, multiplexer_1_out, negator_1_out, shifter_1_out, shifter_2_out;

  Comparator #(.width(5), .mode("unsigned")) comparator_1 (
    .a(float[14:10]), .b(5'b01111), .lt(comparator_1_lt));  // open: gt, eq
  Comparator #(.width(5), .mode("unsigned")) comparator_2 (
    .a(float[14:10]), .b({5{1'b1}}), .eq(comparator_2_eq));  // open: gt, lt
  or or_1 (or_1_out, comparator_1_lt, comparator_2_eq);
  not not_1 (select, or_1_out);
  assign bit_extender_1_out = {{22{1'b0}}, float[9:0]};  // Bit_Extender bit_extender_1
  Adder #(.width(32)) adder_1 (.a(bit_extender_1_out), .b(32'h400), .out(adder_1_out));  // open: cin, cout
  Multiplexer #(.width(32), .enable("false")) multiplexer_1 (
    .in0({32{1'b0}}), .in1(adder_1_out), .out(multiplexer_1_out), .sel(select));
  Subtractor #(.width(5)) subtractor_1 (.a(float[14:10]), .b(5'b01111), .out(subtractor_1_out));  // open: bin, bout
  Shifter #(.width(32)) shifter_1 (.in(multiplexer_1_out), .\dist (subtractor_1_out), .out(shifter_1_out));
  Shifter #(.width(32), .shift("lr")) shifter_2 (.in(shifter_1_out), .\dist (5'b01010), .out(shifter_2_out));
  Negator #(.width(32)) negator_1 (.in(shifter_2_out), .out(negator_1_out));
  Multiplexer #(.width(32), .enable("false")) multiplexer_2 (
    .in0(negator_1_out), .in1(shifter_2_out), .out(\int ), .sel(not_2_out));
  not not_2 (not_2_out, float[15]);

  // Other names for the same wires on the sheet: fraction[9:0] = float[9:0]; exponent[4:0] = float[14:10];
  //   sign = float[15]
endmodule
