// Logisim project grf.circ as structural Verilog: 1 circuit, main circuit grf
module grf (
  input  in_1,
  input  reset,
  input  WE,
  input  [4:0] A1,
  input  [4:0] A2,
  input  [31:0] WD,
  input  [4:0] A3,
  output [31:0] RD1,
  output [31:0] RD2
);

  wire [31:0] input_1, input_2, input_3, input_4, input_5, input_6, input_7, input_8, input_9, input_10,
       input_11, input_12, input_13, input_14, input_15, input_16, input_17, input_18, input_19, input_20,
       input_21, input_22, input_23, input_24, input_25, input_26, input_27, input_28, input_29, input_30,
       input_31, Output_0, Output_1, Output_2, Output_3, Output_4, Output_5, Output_6, Output_7, Output_8,
       Output_9, Output_10, Output_11, Output_12, Output_13, Output_14, Output_15, Output_16, Output_17,
       Output_18, Output_19, Output_20, Output_21, Output_22, Output_23, Output_24, Output_25, Output_26,
       Output_27, Output_28, Output_29, Output_30, Output_31;

  Register #(.width(32)) register_1 (.D({32{1'b0}}), .en(WE), .Q(Output_0), .clk(in_1), .clr(reset));
  Register #(.width(32)) register_2 (.D(input_4), .en(WE), .Q(Output_4), .clk(in_1), .clr(reset));
  Register #(.width(32)) register_3 (.D(input_8), .en(WE), .Q(Output_8), .clk(in_1), .clr(reset));
  Register #(.width(32)) register_4 (.D(input_12), .en(WE), .Q(Output_12), .clk(in_1), .clr(reset));
  Register #(.width(32)) register_5 (.D(input_16), .en(WE), .Q(Output_16), .clk(in_1), .clr(reset));
  Register #(.width(32)) register_6 (.D(input_20), .en(WE), .Q(Output_20), .clk(in_1), .clr(reset));
  Register #(.width(32)) register_7 (.D(input_24), .en(WE), .Q(Output_24), .clk(in_1), .clr(reset));
  Register #(.width(32)) register_8 (.D(input_28), .en(WE), .Q(Output_28), .clk(in_1), .clr(reset));
  Register #(.width(32)) register_9 (.D(input_1), .en(WE), .Q(Output_1), .clk(in_1), .clr(reset));
  Register #(.width(32)) register_10 (.D(input_5), .en(WE), .Q(Output_5), .clk(in_1), .clr(reset));
  Register #(.width(32)) register_11 (.D(input_9), .en(WE), .Q(Output_9), .clk(in_1), .clr(reset));
  Register #(.width(32)) register_12 (.D(input_13), .en(WE), .Q(Output_13), .clk(in_1), .clr(reset));
  Register #(.width(32)) register_13 (.D(input_17), .en(WE), .Q(Output_17), .clk(in_1), .clr(reset));
  Register #(.width(32)) register_14 (.D(input_21), .en(WE), .Q(Output_21), .clk(in_1), .clr(reset));
  Register #(.width(32)) register_15 (.D(input_25), .en(WE), .Q(Output_25), .clk(in_1), .clr(reset));
  Register #(.width(32)) register_16 (.D(input_29), .en(WE), .Q(Output_29), .clk(in_1), .clr(reset));
  Register #(.width(32)) register_17 (.D(input_2), .en(WE), .Q(Output_2), .clk(in_1), .clr(reset));
  Register #(.width(32)) register_18 (.D(input_6), .en(WE), .Q(Output_6), .clk(in_1), .clr(reset));
  Register #(.width(32)) register_19 (.D(input_10), .en(WE), .Q(Output_10), .clk(in_1), .clr(reset));
  Register #(.width(32)) register_20 (.D(input_14), .en(WE), .Q(Output_14), .clk(in_1), .clr(reset));
  Register #(.width(32)) register_21 (.D(input_18), .en(WE), .Q(Output_18), .clk(in_1), .clr(reset));
  Register #(.width(32)) register_22 (.D(input_22), .en(WE), .Q(Output_22), .clk(in_1), .clr(reset));
  Register #(.width(32)) register_23 (.D(input_26), .en(WE), .Q(Output_26), .clk(in_1), .clr(reset));
  Register #(.width(32)) register_24 (.D(input_30), .en(WE), .Q(Output_30), .clk(in_1), .clr(reset));
  Register #(.width(32)) register_25 (.D(input_3), .en(WE), .Q(Output_3), .clk(in_1), .clr(reset));
  Register #(.width(32)) register_26 (.D(input_7), .en(WE), .Q(Output_7), .clk(in_1), .clr(reset));
  Register #(.width(32)) register_27 (.D(input_11), .en(WE), .Q(Output_11), .clk(in_1), .clr(reset));
  Register #(.width(32)) register_28 (.D(input_15), .en(WE), .Q(Output_15), .clk(in_1), .clr(reset));
  Register #(.width(32)) register_29 (.D(input_19), .en(WE), .Q(Output_19), .clk(in_1), .clr(reset));
  Register #(.width(32)) register_30 (.D(input_23), .en(WE), .Q(Output_23), .clk(in_1), .clr(reset));
  Register #(.width(32)) register_31 (.D(input_27), .en(WE), .Q(Output_27), .clk(in_1), .clr(reset));
  Register #(.width(32)) register_32 (.D(input_31), .en(WE), .Q(Output_31), .clk(in_1), .clr(reset));
  Multiplexer #(.select(5), .width(32), .disabled(0), .enable("false")) multiplexer_1 (
    .in0(Output_0), .in1(Output_1), .in2(Output_2), .in3(Output_3), .in4(Output_4), .in5(Output_5),
    .in6(Output_6), .in7(Output_7), .in8(Output_8), .in9(Output_9), .in10(Output_10), .in11(Output_11),
    .in12(Output_12), .in13(Output_13), .in14(Output_14), .in15(Output_15), .in16(Output_16),
    .in17(Output_17), .in18(Output_18), .in19(Output_19), .in20(Output_20), .in21(Output_21),
    .in22(Output_22), .in23(Output_23), .in24(Output_24), .in25(Output_25), .in26(Output_26),
    .in27(Output_27), .in28(Output_28), .in29(Output_29), .in30(Output_30), .in31(Output_31), .out(RD1),
    .sel(A1));
  Multiplexer #(.select(5), .width(32), .disabled(0), .enable("false")) multiplexer_2 (
    .in0(Output_0), .in1(Output_1), .in2(Output_2), .in3(Output_3), .in4(Output_4), .in5(Output_5),
    .in6(Output_6), .in7(Output_7), .in8(Output_8), .in9(Output_9), .in10(Output_10), .in11(Output_11),
    .in12(Output_12), .in13(Output_13), .in14(Output_14), .in15(Output_15), .in16(Output_16),
    .in17(Output_17), .in18(Output_18), .in19(Output_19), .in20(Output_20), .in21(Output_21),
    .in22(Output_22), .in23(Output_23), .in24(Output_24), .in25(Output_25), .in26(Output_26),
    .in27(Output_27), .in28(Output_28), .in29(Output_29), .in30(Output_30), .in31(Output_31), .out(RD2),
    .sel(A2));
  Demultiplexer #(.select(5), .width(32), .tristate("true"), .disabled(0), .enable("false")) demultiplexer_1 (
    .out1(input_1), .out2(input_2), .out3(input_3), .out4(input_4), .out5(input_5), .out6(input_6),
    .out7(input_7), .out8(input_8), .out9(input_9), .out10(input_10), .out11(input_11), .out12(input_12),
    .out13(input_13), .out14(input_14), .out15(input_15), .out16(input_16), .out17(input_17),
    .out18(input_18), .out19(input_19), .out20(input_20), .out21(input_21), .out22(input_22),
    .out23(input_23), .out24(input_24), .out25(input_25), .out26(input_26), .out27(input_27),
    .out28(input_28), .out29(input_29), .out30(input_30), .out31(input_31), .in(WD), .sel(A3));  // open: out0

  // Other names for the same wires on the sheet: clk = in_1
endmodule
