// Logisim project logisim_swap.circ as structural Verilog: 2 circuits, main circuit main
module main (
  input  l1,
  input  l2,
  input  s,
  output o1,
  output o2
);

  wire and_1_out, and_3_out, not_1_out;

  not not_1 (not_1_out, s);
  and and_1 (and_1_out, l1, not_1_out);
  and and_2 (and_1_out, l2, s);
  and and_3 (and_3_out, l1, s);
  and and_4 (and_3_out, l2, not_1_out);
  buf or_1 (o2, and_3_out);  // OR_Gate
  buf or_2 (o1, and_1_out);  // OR_Gate
endmodule

module swap (
  input  l1,
  input  l2,
  input  s,
  output o1,
  output o2
);

  wire and_1_out, and_2_out, and_3_out, and_4_out, not_1_out, not_2_out;

  not not_1 (not_1_out, s);
  not not_2 (not_2_out, s);
  and and_1 (and_1_out, l2, s);
  and and_2 (and_2_out, l1, not_1_out);
  and and_3 (and_3_out, l2, not_2_out);
  and and_4 (and_4_out, l1, s);
  or or_1 (o1, and_1_out, and_2_out);
  or or_2 (o2, and_3_out, and_4_out);
endmodule
