// Logisim project navigation.circ as structural Verilog: 3 circuits, main circuit navigation
module navigation (
  input  [1:0] dir,
  input  clk,
  input  reset,
  output arrive,
  output hit
);

  wire \状态转移_1_hit ;
  wire [2:0] \循环状态寄存器_q , \状态转移_1_d0 ;

  \状态转移  \u_状态转移_1  (
    .input_1(dir[1]), .input_0(dir[0]), .Q2(\循环状态寄存器_q [2]), .Q1(\循环状态寄存器_q [1]), .Q0(\循环状态寄存器_q [0]),
    .D2(\状态转移_1_d0 [2]), .D1(\状态转移_1_d0 [1]), .D0(\状态转移_1_d0 [0]), .hit(\状态转移_1_hit ));
  Register #(.width(3)) \u_循环状态寄存器  (.D(\状态转移_1_d0 ), .Q(\循环状态寄存器_q ), .clk(clk), .clr(reset));  // open: en
  Register #(.width(1)) \hit状态寄存器  (.D(\状态转移_1_hit ), .Q(hit), .clk(clk), .clr(reset));  // open: en
  \输出逻辑  \u_输出逻辑_1  (.Q2(\循环状态寄存器_q [2]), .Q1(\循环状态寄存器_q [1]), .Q0(\循环状态寄存器_q [0]), .arrive(arrive));
endmodule

module \状态转移  (
  input  input_1,
  input  input_0,
  input  Q2,
  input  Q1,
  input  Q0,
  output D2,
  output D1,
  output D0,
  output hit
);

  wire and_1_out, and_2_out, and_3_out, and_4_out, and_5_out, and_6_out, and_7_out, and_8_out, and_9_out,
       and_10_out, and_11_out, and_12_out, and_13_out, and_14_out, and_15_out, and_16_out, and_17_out,
       and_18_out, and_19_out, not_1_out, not_2_out, not_3_out, not_4_out, not_5_out, not_6_out, not_7_out,
       not_8_out, not_9_out, not_10_out, not_11_out, not_12_out, not_13_out, not_14_out, not_15_out,
       not_16_out, not_17_out, not_18_out, not_19_out, not_20_out, not_21_out, not_22_out, not_23_out,
       not_24_out, not_25_out, not_26_out, not_27_out, not_28_out, not_29_out;

  not not_1 (not_1_out, input_1);
  not not_2 (not_2_out, input_0);
  not not_3 (not_3_out, Q0);
  not not_4 (not_4_out, input_1);
  not not_5 (not_5_out, input_1);
  not not_6 (not_6_out, input_0);
  not not_7 (not_7_out, input_1);
  not not_8 (not_8_out, Q1);
  not not_9 (not_9_out, input_1);
  not not_10 (not_10_out, Q0);
  not not_11 (not_11_out, input_0);
  not not_12 (not_12_out, Q0);
  not not_13 (not_13_out, input_1);
  not not_14 (not_14_out, input_0);
  not not_15 (not_15_out, Q2);
  not not_16 (not_16_out, Q1);
  not not_17 (not_17_out, input_0);
  not not_18 (not_18_out, input_1);
  not not_19 (not_19_out, input_0);
  not not_20 (not_20_out, Q2);
  not not_21 (not_21_out, input_1);
  not not_22 (not_22_out, Q2);
  not not_23 (not_23_out, Q0);
  not not_24 (not_24_out, Q2);
  not not_25 (not_25_out, Q1);
  not not_26 (not_26_out, Q0);
  not not_27 (not_27_out, input_0);
  not not_28 (not_28_out, Q2);
  not not_29 (not_29_out, Q0);
  and and_1 (and_1_out, not_1_out, not_2_out, Q1, not_3_out);
  and and_2 (and_2_out, not_4_out, input_0, Q1, Q0);
  and and_3 (and_3_out, input_0, Q2, Q0);
  and and_4 (and_4_out, input_0, Q2, Q1);
  and and_5 (and_5_out, not_5_out, not_6_out, Q0);
  and and_6 (and_6_out, not_7_out, not_8_out, Q0);
  and and_7 (and_7_out, not_9_out, input_0, Q1, not_10_out);
  and and_8 (and_8_out, input_1, not_11_out, Q1, not_12_out);
  and and_9 (and_9_out, input_1, input_0, Q1, Q0);
  and and_10 (and_10_out, not_13_out, not_14_out, not_15_out, not_16_out);
  and and_11 (and_11_out, not_17_out, Q1, Q0);
  and and_12 (and_12_out, input_1, input_0, Q0);
  and and_13 (and_13_out, input_1, input_0, Q1);
  and and_14 (and_14_out, not_18_out, not_19_out, not_20_out, Q1, Q0);
  and and_15 (and_15_out, not_21_out, input_0, not_22_out, not_23_out);
  and and_16 (and_16_out, input_0, not_24_out, not_25_out, not_26_out);
  and and_17 (and_17_out, input_0, Q2, Q1);
  and and_18 (and_18_out, input_1, not_27_out, not_28_out, not_29_out);
  and and_19 (and_19_out, input_1, input_0, Q0);
  or or_1 (D2, and_1_out, and_2_out, and_3_out, and_4_out);
  or or_2 (D1, and_5_out, and_6_out, and_7_out, and_8_out, and_9_out);
  or or_3 (D0, and_10_out, and_11_out, and_12_out, and_13_out);
  or or_4 (hit, and_14_out, and_15_out, and_16_out, and_17_out, and_18_out, and_19_out);
endmodule

module \输出逻辑  (
  input  Q2,
  input  Q1,
  input  Q0,
  output arrive
);

  wire not_1_out, not_2_out;

  not not_1 (not_1_out, Q1);
  not not_2 (not_2_out, Q0);
  and and_1 (arrive, Q2, not_1_out, not_2_out);
endmodule
