// Logisim project P3.circ as structural Verilog: 9 circuits, main circuit main
module main (
  input  Reset,
  output [31:0] out_2,
  output [31:0] out_3,
  output out_4,
  output [4:0] out_5,
  output [31:0] out_6,
  output out_7,
  output [31:0] out_8,
  output [31:0] out_9
);

  wire alu_1_zero, ALUSrc, Clk;
  wire [1:0] ALUOp, EXTOp, MemtoReg, NPCOp, RegDst;
  wire [31:0] dm_1_readdata, ext_1_extimm, grf_1_rd1, multiplexer_2_out, PC_4;

  Clock u_Clk (.out(Clk));
  IFU ifu_1 (
    .Clk(Clk), .Reset(Reset), .Imm(out_2[25:0]), .NPCOp(NPCOp), .Zero(alu_1_zero), .PC(out_3), .Instr(out_2),
    .PC_4(PC_4), .RA(grf_1_rd1));
  Multiplexer #(.select(2), .width(5)) multiplexer_1 (
    .in0(out_2[20:16]), .in1(out_2[15:11]), .in2({5{1'b1}}), .out(out_5), .sel(RegDst));  // open: in3, en
  EXT ext_1 (.Imm16(out_2[15:0]), .ExtOp(EXTOp), .ExtImm(ext_1_extimm));
  Controller controller_1 (
    .opcode(out_2[31:26]), .funct(out_2[5:0]), .NPCOp(NPCOp), .EXTOp(EXTOp), .RegDst(RegDst),
    .RegWrite(out_4), .ALUSrc(ALUSrc), .ALUOp(ALUOp), .MemWrite(out_7), .MemtoReg(MemtoReg));
  GRF grf_1 (
    .A1(out_2[25:21]), .A2(out_2[20:16]), .WD(out_6), .A3(out_5), .RD1(grf_1_rd1), .RD2(out_9), .in_1(Clk),
    .reset(Reset), .WE(out_4));
  Multiplexer #(.width(32)) multiplexer_2 (
    .in0(out_9), .in1(ext_1_extimm), .out(multiplexer_2_out), .sel(ALUSrc));  // open: en
  ALU alu_1 (.SrcA(grf_1_rd1), .SrcB(multiplexer_2_out), .ALUOp(ALUOp), .ALUResult(out_8), .Zero(alu_1_zero));
  DM dm_1 (.ALUResult(out_8), .WriteData(out_9), .MemWrite(out_7), .Clk(Clk), .Reset(Reset), .ReadData(dm_1_readdata));
  Multiplexer #(.select(2), .width(32)) multiplexer_3 (
    .in0(out_8), .in1(dm_1_readdata), .in2(PC_4), .out(out_6), .sel(MemtoReg));  // open: in3, en

  // Other names for the same wires on the sheet: Instr[31:0] = out_2; MemADDr[31:0] = out_8; MemData[31:0] = out_9;
  //   MemWrite = out_7; PC[31:0] = out_3; RegADDr[4:0] = out_5; RegData[31:0] = out_6; RegWrite = out_4
endmodule

module NPC (
  input  [31:0] PC,
  input  [25:0] Imm,
  input  [31:0] RA,
  input  [1:0] NPCOp,
  input  Zero,
  output [31:0] PC_4,
  output [31:0] NPC
);

  wire and_1_out, and_2_out;
  wire [0:0] or_1_out;
  wire [15:0] bit_extender_1_out;
  wire [31:0] adder_2_out, bit_extender_2_out, shifter_1_out, subtractor_1_out;

  Bit_Extender #(.in_width(26)) bit_extender_1 (.in(Imm), .out(bit_extender_1_out));
  assign bit_extender_2_out = {{16{bit_extender_1_out[15]}}, bit_extender_1_out};  // Bit_Extender bit_extender_2
  Adder #(.width(32)) adder_1 (.a(PC), .b(32'h4), .out(PC_4));  // open: cin, cout
  Shifter #(.width(32)) shifter_1 (.in(bit_extender_2_out), .\dist (5'b00010), .out(shifter_1_out));
  and and_1 (and_1_out, NPCOp[0], Zero);
  and and_2 (and_2_out, NPCOp[1], NPCOp[0]);
  Adder #(.width(32)) adder_2 (.a(PC_4), .b(shifter_1_out), .out(adder_2_out));  // open: cin, cout
  or or_1 (or_1_out[0], and_1_out, and_2_out);
  Subtractor #(.width(32)) subtractor_1 (
    .a({PC[31:28], Imm, 2'b00}), .b(32'h3000), .out(subtractor_1_out));  // open: bin, bout
  Multiplexer #(.select(2), .width(32)) multiplexer_1 (
    .in0(PC_4), .in1(adder_2_out), .in2(subtractor_1_out), .in3(RA), .out(NPC), .sel({NPCOp[1], or_1_out[0]}));  // open: en
endmodule

module IFU (
  input  Clk,
  input  Reset,
  input  [25:0] Imm,
  input  [1:0] NPCOp,
  input  Zero,
  input  [31:0] RA,
  output [31:0] PC,
  output [31:0] Instr,
  output [31:0] PC_4
);

  wire [31:0] NPC_npc, PC_q;

  // Probe on NPC_npc
  Register #(.width(32)) u_PC (.D(NPC_npc), .Q(PC_q), .clk(Clk), .clr(Reset));  // open: en
  // Probe on PC_q
  NPC NPC (.PC(PC_q), .Imm(Imm), .RA(RA), .NPCOp(NPCOp), .Zero(Zero), .PC_4(PC_4), .NPC(NPC_npc));
  Adder #(.width(32)) adder_1 (.a(PC_q), .b(32'h3000), .out(PC));  // open: cin, cout
  ROM #(.addrWidth(12), .dataWidth(32)) rom_1 (.addr(PC_q[13:2]), .data(Instr));  // open: sel

  // Notes on the sheet:
  //   contents of rom_1 (hex, n*v repeats v):
  //   341c0000 341d0000 34013456 210820 8c010004 ac010004 3c027878 411822 3c051234 34040005 0 ac85ffff
  //   8c83ffff 10650003 0 10000011 0 34670404 10e3000e 0 3c087777 3508ffff 80022 34001100 e65020 34080000
  //   34090001 340a0001 10a4020 1109fffe c000c22 0 14a5020 1000ffff 14a5020 3e00008
endmodule

module EXT (
  input  [15:0] Imm16,
  input  [1:0] ExtOp,
  output [31:0] ExtImm
);

  wire [31:0] bit_extender_1_out, bit_extender_2_out;

  assign bit_extender_1_out = {{16{1'b0}}, Imm16};  // Bit_Extender bit_extender_1
  assign bit_extender_2_out = {{16{Imm16[15]}}, Imm16};  // Bit_Extender bit_extender_2
  Multiplexer #(.select(2), .width(32)) multiplexer_1 (
    .in0(bit_extender_1_out), .in1(bit_extender_2_out), .in2({Imm16, {16{1'b0}}}), .out(ExtImm), .sel(ExtOp));  // open: in3, en

  // Notes on the sheet:
  //   ExtOp: 00代表0扩展;01代表符号扩展;10代表针对lui把imm16加载到高位
endmodule

module GRF (
  input  in_1,
  input  reset,
  input  WE,
  input  [4:0] A1,
  input  [4:0] A2,
  input  [31:0] WD,
  input  [4:0] A3,
  output [31:0] RD1,
  output [31:0] RD2
);

  wire [31:0] input_1, input_2, input_3, input_4, input_5, input_6, input_7, input_8, input_9, input_10,
       input_11, input_12, input_13, input_14, input_15, input_16, input_17, input_18, input_19, input_20,
       input_21, input_22, input_23, input_24, input_25, input_26, input_27, input_28, input_29, input_30,
       input_31, Output_0, Output_1, Output_2, Output_3, Output_4, Output_5, Output_6, Output_7, Output_8,
       Output_9, Output_10, Output_11, Output_12, Output_13, Output_14, Output_15, Output_16, Output_17,
       Output_18, Output_19, Output_20, Output_21, Output_22, Output_23, Output_24, Output_25, Output_26,
       Output_27, Output_28, Output_29, Output_30, Output_31;

  Register #(.width(32)) register_1 (.D({32{1'b0}}), .en(WE), .Q(Output_0), .clk(in_1), .clr(reset));
  Register #(.width(32)) register_2 (.D(input_4), .en(WE), .Q(Output_4), .clk(in_1), .clr(reset));
  Register #(.width(32)) register_3 (.D(input_8), .en(WE), .Q(Output_8), .clk(in_1), .clr(reset));
  Register #(.width(32)) register_4 (.D(input_12), .en(WE), .Q(Output_12), .clk(in_1), .clr(reset));
  Register #(.width(32)) register_5 (.D(input_16), .en(WE), .Q(Output_16), .clk(in_1), .clr(reset));
  Register #(.width(32)) register_6 (.D(input_20), .en(WE), .Q(Output_20), .clk(in_1), .clr(reset));
  Register #(.width(32)) register_7 (.D(input_24), .en(WE), .Q(Output_24), .clk(in_1), .clr(reset));
  Register #(.width(32)) register_8 (.D(input_28), .en(WE), .Q(Output_28), .clk(in_1), .clr(reset));
  Register #(.width(32)) register_9 (.D(input_1), .en(WE), .Q(Output_1), .clk(in_1), .clr(reset));
  Register #(.width(32)) register_10 (.D(input_5), .en(WE), .Q(Output_5), .clk(in_1), .clr(reset));
  Register #(.width(32)) register_11 (.D(input_9), .en(WE), .Q(Output_9), .clk(in_1), .clr(reset));
  Register #(.width(32)) register_12 (.D(input_13), .en(WE), .Q(Output_13), .clk(in_1), .clr(reset));
  Register #(.width(32)) register_13 (.D(input_17), .en(WE), .Q(Output_17), .clk(in_1), .clr(reset));
  Register #(.width(32)) register_14 (.D(input_21), .en(WE), .Q(Output_21), .clk(in_1), .clr(reset));
  Register #(.width(32)) register_15 (.D(input_25), .en(WE), .Q(Output_25), .clk(in_1), .clr(reset));
  Register #(.width(32)) register_16 (.D(input_29), .en(WE), .Q(Output_29), .clk(in_1), .clr(reset));
  Register #(.width(32)) register_17 (.D(input_2), .en(WE), .Q(Output_2), .clk(in_1), .clr(reset));
  Register #(.width(32)) register_18 (.D(input_6), .en(WE), .Q(Output_6), .clk(in_1), .clr(reset));
  Register #(.width(32)) register_19 (.D(input_10), .en(WE), .Q(Output_10), .clk(in_1), .clr(reset));
  Register #(.width(32)) register_20 (.D(input_14), .en(WE), .Q(Output_14), .clk(in_1), .clr(reset));
  Register #(.width(32)) register_21 (.D(input_18), .en(WE), .Q(Output_18), .clk(in_1), .clr(reset));
  Register #(.width(32)) register_22 (.D(input_22), .en(WE), .Q(Output_22), .clk(in_1), .clr(reset));
  Register #(.width(32)) register_23 (.D(input_26), .en(WE), .Q(Output_26), .clk(in_1), .clr(reset));
  Register #(.width(32)) register_24 (.D(input_30), .en(WE), .Q(Output_30), .clk(in_1), .clr(reset));
  Register #(.width(32)) register_25 (.D(input_3), .en(WE), .Q(Output_3), .clk(in_1), .clr(reset));
  Register #(.width(32)) register_26 (.D(input_7), .en(WE), .Q(Output_7), .clk(in_1), .clr(reset));
  Register #(.width(32)) register_27 (.D(input_11), .en(WE), .Q(Output_11), .clk(in_1), .clr(reset));
  Register #(.width(32)) register_28 (.D(input_15), .en(WE), .Q(Output_15), .clk(in_1), .clr(reset));
  Register #(.width(32)) register_29 (.D(input_19), .en(WE), .Q(Output_19), .clk(in_1), .clr(reset));
  Register #(.width(32)) register_30 (.D(input_23), .en(WE), .Q(Output_23), .clk(in_1), .clr(reset));
  Register #(.width(32)) register_31 (.D(input_27), .en(WE), .Q(Output_27), .clk(in_1), .clr(reset));
  Register #(.width(32)) register_32 (.D(input_31), .en(WE), .Q(Output_31), .clk(in_1), .clr(reset));
  Multiplexer #(.select(5), .width(32), .disabled(0), .enable("false")) multiplexer_1 (
    .in0(Output_0), .in1(Output_1), .in2(Output_2), .in3(Output_3), .in4(Output_4), .in5(Output_5),
    .in6(Output_6), .in7(Output_7), .in8(Output_8), .in9(Output_9), .in10(Output_10), .in11(Output_11),
    .in12(Output_12), .in13(Output_13), .in14(Output_14), .in15(Output_15), .in16(Output_16),
    .in17(Output_17), .in18(Output_18), .in19(Output_19), .in20(Output_20), .in21(Output_21),
    .in22(Output_22), .in23(Output_23), .in24(Output_24), .in25(Output_25), .in26(Output_26),
    .in27(Output_27), .in28(Output_28), .in29(Output_29), .in30(Output_30), .in31(Output_31), .out(RD1),
    .sel(A1));
  Multiplexer #(.select(5), .width(32), .disabled(0), .enable("false")) multiplexer_2 (
    .in0(Output_0), .in1(Output_1), .in2(Output_2), .in3(Output_3), .in4(Output_4), .in5(Output_5),
    .in6(Output_6), .in7(Output_7), .in8(Output_8), .in9(Output_9), .in10(Output_10), .in11(Output_11),
    .in12(Output_12), .in13(Output_13), .in14(Output_14), .in15(Output_15), .in16(Output_16),
    .in17(Output_17), .in18(Output_18), .in19(Output_19), .in20(Output_20), .in21(Output_21),
    .in22(Output_22), .in23(Output_23), .in24(Output_24), .in25(Output_25), .in26(Output_26),
    .in27(Output_27), .in28(Output_28), .in29(Output_29), .in30(Output_30), .in31(Output_31), .out(RD2),
    .sel(A2));
  Demultiplexer #(.select(5), .width(32), .tristate("true"), .disabled(0), .enable("false")) demultiplexer_1 (
    .out1(input_1), .out2(input_2), .out3(input_3), .out4(input_4), .out5(input_5), .out6(input_6),
    .out7(input_7), .out8(input_8), .out9(input_9), .out10(input_10), .out11(input_11), .out12(input_12),
    .out13(input_13), .out14(input_14), .out15(input_15), .out16(input_16), .out17(input_17),
    .out18(input_18), .out19(input_19), .out20(input_20), .out21(input_21), .out22(input_22),
    .out23(input_23), .out24(input_24), .out25(input_25), .out26(input_26), .out27(input_27),
    .out28(input_28), .out29(input_29), .out30(input_30), .out31(input_31), .in(WD), .sel(A3));  // open: out0

  // Other names for the same wires on the sheet: clk = in_1
endmodule

module ALU (
  input  [31:0] SrcA,
  input  [31:0] SrcB,
  input  [1:0] ALUOp,
  output [31:0] ALUResult,
  output Zero
);

  wire [31:0] adder_1_out, subtractor_1_out, \或运算_out ;

  Adder #(.width(32)) adder_1 (.a(SrcA), .b(SrcB), .out(adder_1_out));  // open: cin, cout
  Subtractor #(.width(32)) subtractor_1 (.a(SrcA), .b(SrcB), .out(subtractor_1_out));  // open: bin, bout
  assign \或运算_out  = SrcA | SrcB;  // OR_Gate 或运算, 32 bits wide
  Multiplexer #(.select(2), .width(32)) multiplexer_1 (
    .in0(adder_1_out), .in1(subtractor_1_out), .in2(\或运算_out ), .out(ALUResult), .sel(ALUOp));  // open: in3, en
  Comparator #(.width(32)) comparator_1 (.a(subtractor_1_out), .b({32{1'b0}}), .eq(Zero));  // open: gt, lt

  // Notes on the sheet:
  //   ALUOp 1:0  00为加法,01为减法,10为或运算,11为保留SrcB本身
endmodule

module DM (
  input  [31:0] ALUResult,
  input  [31:0] WriteData,
  input  Reset,
  input  MemWrite,
  input  Clk,
  output [31:0] ReadData
);

  RAM #(.addrWidth(12), .dataWidth(32), .bus("separate")) ram_1 (
    .addr(ALUResult[13:2]), .din(WriteData), .data(ReadData), .str(MemWrite), .clk(Clk), .clr(Reset));  // open: sel, ld

  // Notes on the sheet:
  //   ALUResult:目标数据的地址;WriteData:需要写入的数据;MemWrite:为1时允许写入
endmodule

module Controller (
  input  [5:0] opcode,
  input  [5:0] funct,
  output [1:0] NPCOp,
  output [1:0] EXTOp,
  output [1:0] RegDst,
  output RegWrite,
  output ALUSrc,
  output [1:0] ALUOp,
  output MemWrite,
  output [1:0] MemtoReg
);

  wire add, beq, jr, nop, not_1_out, not_2_out, not_3_out, not_4_out, not_5_out, not_6_out, not_7_out,
       not_8_out, not_9_out, not_10_out, not_11_out, not_12_out, ori, RType_out, sub;

  not not_1 (not_1_out, opcode[5]);
  not not_2 (not_2_out, opcode[4]);
  not not_3 (not_3_out, opcode[3]);
  or or_1 (NPCOp[1], jr, MemtoReg[1]);
  or or_2 (NPCOp[0], beq, jr);
  not not_4 (not_4_out, opcode[1]);
  not not_5 (not_5_out, opcode[2]);
  not not_6 (not_6_out, opcode[0]);
  or or_3 (EXTOp[0], MemtoReg[0], MemWrite);
  or or_4 (RegDst[0], add, sub);
  and RType (RType_out, not_1_out, not_2_out, not_3_out, not_5_out, not_4_out, not_6_out);
  and _001101 (ori, not_1_out, not_2_out, opcode[3], opcode[2], not_4_out, opcode[0]);
  and _100011 (MemtoReg[0], opcode[5], not_2_out, not_3_out, not_5_out, opcode[1], opcode[0]);
  and _101011 (MemWrite, opcode[5], not_2_out, opcode[3], not_5_out, opcode[1], opcode[0]);
  and _000100 (beq, not_1_out, not_2_out, not_3_out, opcode[2], not_4_out, not_6_out);
  and _001111 (EXTOp[1], not_1_out, not_2_out, opcode[3], opcode[2], opcode[1], opcode[0]);
  and _000011 (MemtoReg[1], not_1_out, not_2_out, not_3_out, not_5_out, opcode[1], opcode[0]);
  or or_5 (RegWrite, ori, add, sub, MemtoReg[0], EXTOp[1], MemtoReg[1]);
  or or_6 (ALUSrc, ori, MemtoReg[0], MemWrite, EXTOp[1]);
  or or_7 (ALUOp[1], ori, EXTOp[1]);
  or or_8 (ALUOp[0], sub, beq);
  not not_7 (not_7_out, funct[5]);
  not not_8 (not_8_out, funct[4]);
  not not_9 (not_9_out, funct[3]);
  not not_10 (not_10_out, funct[2]);
  not not_11 (not_11_out, funct[1]);
  not not_12 (not_12_out, funct[0]);
  and _100000 (add, funct[5], not_8_out, not_9_out, not_10_out, not_11_out, not_12_out, RType_out);
  and _100010 (sub, funct[5], not_8_out, not_9_out, not_10_out, funct[1], not_12_out, RType_out);
  and _000000 (nop, not_7_out, not_8_out, not_9_out, not_10_out, not_11_out, not_12_out, RType_out);
  and _001000 (jr, not_7_out, not_8_out, funct[3], not_10_out, not_11_out, not_12_out, RType_out);

  assign RegDst[1] = MemtoReg[1];

  // Other names for the same wires on the sheet: lui = EXTOp[1]; lw = MemtoReg[0]; jal = MemtoReg[1]; op0 = opcode[0];
  //   op1 = opcode[1]; op2 = opcode[2]; op3 = opcode[3]; op4 = opcode[4]; op5 = opcode[5]; sw = MemWrite
endmodule

module test (
  input  NPCOp2,
  input  NPCOp1,
  input  zero,
  output select2,
  output select1
);

  wire and_1_out, and_2_out;

  and and_1 (and_1_out, NPCOp1, zero);
  and and_2 (and_2_out, NPCOp2, NPCOp1);
  or or_1 (select1, and_1_out, and_2_out);

  assign select2 = NPCOp2;
endmodule
